# Fritzing sketch Bus_timer (saved by Fritzing 0.9.3b)
circuit board: 7.2cm x 4.75cm
breadboards: 1

parts:
  IC1 = MCP23017 I2C I/O Expander
  7Seg1 = 7 Segment Display
  7Seg6 = 7 Segment Display
  7Seg7 = 7 Segment Display
  7Seg8 = 7 Segment Display
  R1 = Resistor [tolerance=±5% resistance=100 package=THT]
  R2 = Resistor [tolerance=±5% resistance=100 package=THT]
  R3 = Resistor [tolerance=±5% resistance=100 package=THT]
  R4 = Resistor [tolerance=±5% resistance=100 package=THT]
  R5 = Resistor [tolerance=±5% resistance=100 package=THT]
  R6 = Resistor [tolerance=±5% resistance=100 package=THT]
  R7 = Resistor [tolerance=±5% resistance=100 package=THT]
  R8 = Resistor [tolerance=±5% resistance=100 package=THT]
  J1 = female pin header, 9 pins [form="♀ (female)"]
  R9 = Resistor [tolerance=±5% resistance=10k package=THT]
  R10 = Resistor [tolerance=±5% resistance=4.7k package=THT]
  R11 = Resistor [tolerance=±5% resistance=4.7k package=THT]
  MODE_SW = Pushbutton [package="[THT]"]
  7Seg5 = 7 Segment Display
  R12 = Resistor [tolerance=±5% resistance=47k package=THT]
  Q8 = NPN-Transistor [package="TO92 [THT]"]
  Q7 = NPN-Transistor [package="TO92 [THT]"]
  Q6 = NPN-Transistor [package="TO92 [THT]"]
  Q5 = NPN-Transistor [package="TO92 [THT]"]
  Q2 = NPN-Transistor [package="TO92 [THT]"]
  Q1 = NPN-Transistor [package="TO92 [THT]"]
  J2 = female pin header, 5 pins [form="♀ (female)"]
  7Seg2 = 7 Segment Display
  Q4 = NPN-Transistor [package="TO92 [THT]"]
  7Seg3 = 7 Segment Display
  7Seg4 = 7 Segment Display
  Q3 = NPN-Transistor [package="TO92 [THT]"]

nets (from the schematic view):
  GPB0: IC1.GPB0, Q1.B
  GPB1: IC1.GPB1, Q2.B
  GPB2: IC1.GPB2, Q3.B
  GPB3: IC1.GPB3, Q4.B
  GPB4: IC1.GPB4, Q5.B
  GPB5: IC1.GPB5, Q6.B
  GPB6: IC1.GPB6, Q7.B
  GPB7: IC1.GPB7, Q8.B
  3.3V: IC1.VDD, J1.pin2, R9.Pin_1, R10.Pin_1, R11.Pin_1, R12.Pin_1
  GND: IC1.VSS, IC1.A0, IC1.A1, IC1.A2, J1.pin1, MODE_SW.Pin_3, MODE_SW.Pin_4, Q8.E, Q7.E, Q6.E, Q5.E, Q2.E, Q1.E, J2.pin1, J2.pin4, Q4.E, Q3.E
  SCL: IC1.SCL, J1.pin3, R10.Pin_0
  SDA: IC1.SDA, J1.pin4, R11.Pin_0
  N1: IC1.RESET, R9.Pin_0
  N2: IC1.GPA0, R1.Pin_1
  N3: IC1.GPA1, R2.Pin_1
  N4: IC1.GPA2, R3.Pin_1
  N5: IC1.GPA3, R4.Pin_1
  N6: IC1.GPA4, R5.Pin_1
  N7: IC1.GPA5, R6.Pin_1
  N8: IC1.GPA6, R7.Pin_1
  N9: IC1.GPA7, R8.Pin_1
  N10: 7Seg1.Segment_A#1, 7Seg6.Segment_A#1, 7Seg7.Segment_A#1, 7Seg8.Segment_A#1, R7.Pin_0, 7Seg5.Segment_A#1, 7Seg2.Segment_A#1, 7Seg3.Segment_A#1, 7Seg4.Segment_A#1
  N11: 7Seg1.Segment_F, 7Seg6.Segment_F, 7Seg7.Segment_F, 7Seg8.Segment_F, R5.Pin_0, 7Seg5.Segment_F, 7Seg2.Segment_F, 7Seg3.Segment_F, 7Seg4.Segment_F
  N12: 7Seg1.Segment_E, 7Seg6.Segment_E, 7Seg7.Segment_E, 7Seg8.Segment_E, R6.Pin_0, 7Seg5.Segment_E, 7Seg2.Segment_E, 7Seg3.Segment_E, 7Seg4.Segment_E
  N13: 7Seg1.Segment_D, 7Seg6.Segment_D, 7Seg7.Segment_D, 7Seg8.Segment_D, R1.Pin_0, 7Seg5.Segment_D, 7Seg2.Segment_D, 7Seg3.Segment_D, 7Seg4.Segment_D
  N14: 7Seg1.Segment_DP, 7Seg6.Segment_DP, 7Seg7.Segment_DP, 7Seg8.Segment_DP, R8.Pin_0, 7Seg5.Segment_DP, 7Seg2.Segment_DP, 7Seg3.Segment_DP, 7Seg4.Segment_DP
  N15: 7Seg1.Segment_C, 7Seg6.Segment_C, 7Seg7.Segment_C, 7Seg8.Segment_C, R2.Pin_0, 7Seg5.Segment_C, 7Seg2.Segment_C, 7Seg3.Segment_C, 7Seg4.Segment_C
  N16: 7Seg1.common_cathode, Q1.C
  N17: 7Seg1.Segment_B, 7Seg6.Segment_B, 7Seg7.Segment_B, 7Seg8.Segment_B, R3.Pin_0, 7Seg5.Segment_B, 7Seg2.Segment_B, 7Seg3.Segment_B, 7Seg4.Segment_B
  N18: 7Seg1.Segment_A#10, 7Seg6.Segment_A#10, 7Seg7.Segment_A#10, 7Seg8.Segment_A#10, R4.Pin_0, 7Seg5.Segment_A#10, 7Seg2.Segment_A#10, 7Seg3.Segment_A#10, 7Seg4.Segment_A#10
  N19: 7Seg6.common_cathode, Q6.C
  N20: 7Seg7.common_cathode, Q7.C
  N21: 7Seg8.common_cathode, Q8.C
  SW: J1.pin5, MODE_SW.Pin_1, MODE_SW.Pin_2, R12.Pin_0
  N22: 7Seg5.common_cathode, Q5.C
  N23: Q2.C, 7Seg2.common_cathode
  N24: Q4.C, 7Seg4.common_cathode
  N25: 7Seg3.common_cathode, Q3.C

custom parts:
  MCP23017 I2C I/O Expander: The MCP23017 uses two i2c pins (these can be shared with other i2c devices), and in exchange gives you 16 general purpose pins. You can set each of 16 pins to be input, output, input with a pullup or open drain. There's even the ability to get an interrupt via an external pin when any of the inputs change so you don't have to keep polling the chip.
